# Fritzing sketch LED_pushBytton_Arduino (saved by Fritzing 1.0.5)
breadboards: 1

parts:
  Part1 = Arduino Uno (Rev3) - ICSP
  S1 = Pushbutton [package="[THT]"]
  LED1 = LED - 3mm [color="Red (633nm)" current=0.030A package="3 mm [THT]"]
  R1 = Resistor [tolerance=±5% resistance=220 package="2010 [SMD]"]
  R2 = Resistor [tolerance=±5% resistance=220 package="2512 [SMD]"]

nets:
  N1: Part1.GND, S1.Pin_1, S1.Pin_2, R1.Pin_0, R2.Pin_0
  N2: Part1.D3_PWM, S1.Pin_3, S1.Pin_4, R2.Pin_1
  N3: Part1.D4, LED1.anode
  N4: LED1.cathode, R1.Pin_1
